# Fritzing sketch Mic (saved by Fritzing 0.9.3b)
breadboards: 1

parts:
  Raspberry_Pi_1 = Raspberry Pi 3 [part_number=RPI-3-V1.2]
  MCP1 = MCP3208

nets:
  3V3: Raspberry_Pi_1.3v3, MCP1.VREF, MCP1.VDD
  N1: Raspberry_Pi_1.GND, MCP1.DGND, MCP1.AGND
  N2: Raspberry_Pi_1.GPIO10, MCP1.DIN
  N3: Raspberry_Pi_1.GPIO9, MCP1.DOUT
  N4: Raspberry_Pi_1.GPIO11, MCP1.CLK
  N5: Raspberry_Pi_1.GPIO8, MCP1.CS/SHDN
